// Logisim project OTP-DE.circ as structural Verilog: 4 circuits, main circuit main
// 8
module main (
  input  in_1,
  output out_2,
  output [3:0] out_3,
  output [3:0] out_4,
  output [3:0] out_5,
  output [3:0] out_6
);

  wire and_1_out, and_2_out, bcd2led_1_a, bcd2led_1_b, bcd2led_1_c, bcd2led_1_d, bcd2led_1_e, bcd2led_1_f,
       bcd2led_1_g, bcd2led_2_a, bcd2led_2_b, bcd2led_2_c, bcd2led_2_d, bcd2led_2_e, bcd2led_2_f,
       bcd2led_2_g, bcd2led_3_a, bcd2led_3_b, bcd2led_3_c, bcd2led_3_d, bcd2led_3_e, bcd2led_3_f,
       bcd2led_3_g, bcd2led_4_a, bcd2led_4_b, bcd2led_4_c, bcd2led_4_d, bcd2led_4_e, bcd2led_4_f,
       bcd2led_4_g, button_1_out, comparator_1_eq, comparator_2_eq, comparator_3_eq, comparator_4_eq, D0_out,
       D1_out, D2_out, D3_out, d_ff_1_q, D_out, FL_2_out, FL_3_out, FL_4_out, FL_out, multiplexer_1_out,
       multiplexer_2_out, multiplexer_3_out, multiplexer_4_out, multiplexer_5_out, multiplexer_6_out,
       multiplexer_7_out, multiplexer_8_out, multiplexer_9_out, multiplexer_10_out, multiplexer_11_out,
       multiplexer_12_out, multiplexer_13_out, multiplexer_14_out, multiplexer_15_out, multiplexer_16_out;
  wire [3:0] counter_1_q, counter_2_q, counter_3_q, counter_4_q, DCH0_bcd0, DCH1_bcd0, DCH2_bcd0, DCH3_bcd0;

  Clock #(.lowDuration(75)) D (.out(D_out));
  and and_1 (and_1_out, D_out, in_1);
  or or_1 (out_2, D_out, and_1_out);
  xor FL (FL_out, out_3[3], out_3[2]);
  Multiplexer multiplexer_1 (.in0(FL_out), .in1(1'b1), .out(multiplexer_1_out), .sel(in_1));  // open: en
  D_Flip_Flop Q3 (.clk(out_2), .D(multiplexer_2_out), .Q(out_3[3]));  // open: Qn, preset, en, reset
  LED led_1 (.in(out_3[3]));
  D_Flip_Flop d_ff_1 (.clk(button_1_out), .D(and_2_out), .Q(d_ff_1_q), .reset(D_out));  // open: Qn, preset, en
  D_Flip_Flop Q2 (.clk(out_2), .D(multiplexer_3_out), .Q(out_3[2]));  // open: Qn, preset, en, reset
  Multiplexer multiplexer_2 (.in0(out_3[2]), .in1(1'b0), .out(multiplexer_2_out), .sel(in_1));  // open: en
  LED led_2 (.in(out_3[2]));
  Multiplexer multiplexer_3 (.in0(out_3[1]), .in1(1'b0), .out(multiplexer_3_out), .sel(in_1));  // open: en
  DCHandlingFixed DCH3 (
    .B0(out_3[0]), .B1(out_3[1]), .B2(out_3[2]), .B3(out_3[3]), .BCD3(DCH3_bcd0[3]), .BCD2(DCH3_bcd0[2]),
    .BCD1(DCH3_bcd0[1]), .BCD0(DCH3_bcd0[0]));
  BCD2LED bcd2led_1 (
    .B3(DCH3_bcd0[3]), .B2(DCH3_bcd0[2]), .B1(DCH3_bcd0[1]), .B0(DCH3_bcd0[0]), .a(bcd2led_1_a),
    .b(bcd2led_1_b), .c(bcd2led_1_c), .d(bcd2led_1_d), .e(bcd2led_1_e), .f(bcd2led_1_f), .g(bcd2led_1_g));
  _7_Segment_Display u_7_segment_display_1 (
    .g(bcd2led_1_g), .f(bcd2led_1_f), .a(bcd2led_1_a), .b(bcd2led_1_b), .e(bcd2led_1_e), .d(bcd2led_1_d),
    .c(bcd2led_1_c), .dp(1'b0));
  Hex_Digit_Display hex_digit_display_1 (.value(counter_1_q), .dp(1'b0));
  Counter #(.width(4), .max('h9)) counter_1 (
    .Q(counter_1_q), .clk(D3_out), .clr(D_out));  // open: load, D, count, carry
  Button D3 (.out(D3_out));
  D_Flip_Flop Q1 (.clk(out_2), .D(multiplexer_4_out), .Q(out_3[1]));  // open: Qn, preset, en, reset
  Multiplexer multiplexer_4 (.in0(out_3[0]), .in1(1'b1), .out(multiplexer_4_out), .sel(in_1));  // open: en
  LED led_3 (.in(out_3[1]));
  DCHandlingFixed DCH2 (
    .B0(out_4[0]), .B1(out_4[1]), .B2(out_4[2]), .B3(out_4[3]), .BCD3(DCH2_bcd0[3]), .BCD2(DCH2_bcd0[2]),
    .BCD1(DCH2_bcd0[1]), .BCD0(DCH2_bcd0[0]));
  _7_Segment_Display u_7_segment_display_2 (
    .g(bcd2led_2_g), .f(bcd2led_2_f), .a(bcd2led_2_a), .b(bcd2led_2_b), .e(bcd2led_2_e), .d(bcd2led_2_d),
    .c(bcd2led_2_c), .dp(1'b0));
  Hex_Digit_Display hex_digit_display_2 (.value(counter_2_q), .dp(1'b0));
  Counter #(.width(4), .max('h9)) counter_2 (
    .Q(counter_2_q), .clk(D2_out), .clr(D_out));  // open: load, D, count, carry
  Button D2 (.out(D2_out));
  D_Flip_Flop Q0 (.clk(out_2), .D(multiplexer_1_out), .Q(out_3[0]));  // open: Qn, preset, en, reset
  LED led_4 (.in(out_3[0]));
  BCD2LED bcd2led_2 (
    .B3(DCH2_bcd0[3]), .B2(DCH2_bcd0[2]), .B1(DCH2_bcd0[1]), .B0(DCH2_bcd0[0]), .a(bcd2led_2_a),
    .b(bcd2led_2_b), .c(bcd2led_2_c), .d(bcd2led_2_d), .e(bcd2led_2_e), .f(bcd2led_2_f), .g(bcd2led_2_g));
  _7_Segment_Display u_7_segment_display_3 (
    .g(bcd2led_3_g), .f(bcd2led_3_f), .a(bcd2led_3_a), .b(bcd2led_3_b), .e(bcd2led_3_e), .d(bcd2led_3_d),
    .c(bcd2led_3_c), .dp(1'b0));
  Hex_Digit_Display hex_digit_display_3 (.value(counter_3_q), .dp(1'b0));
  Button D1 (.out(D1_out));
  DCHandlingFixed DCH1 (
    .B0(out_5[0]), .B1(out_5[1]), .B2(out_5[2]), .B3(out_5[3]), .BCD3(DCH1_bcd0[3]), .BCD2(DCH1_bcd0[2]),
    .BCD1(DCH1_bcd0[1]), .BCD0(DCH1_bcd0[0]));
  BCD2LED bcd2led_3 (
    .B3(DCH1_bcd0[3]), .B2(DCH1_bcd0[2]), .B1(DCH1_bcd0[1]), .B0(DCH1_bcd0[0]), .a(bcd2led_3_a),
    .b(bcd2led_3_b), .c(bcd2led_3_c), .d(bcd2led_3_d), .e(bcd2led_3_e), .f(bcd2led_3_f), .g(bcd2led_3_g));
  Counter #(.width(4), .max('h9)) counter_3 (
    .Q(counter_3_q), .clk(D1_out), .clr(D_out));  // open: load, D, count, carry
  xor FL_2 (FL_2_out, out_4[3], out_4[2]);
  Multiplexer multiplexer_5 (.in0(FL_2_out), .in1(1'b0), .out(multiplexer_5_out), .sel(in_1));  // open: en
  DCHandlingFixed DCH0 (
    .B0(out_6[0]), .B1(out_6[1]), .B2(out_6[2]), .B3(out_6[3]), .BCD3(DCH0_bcd0[3]), .BCD2(DCH0_bcd0[2]),
    .BCD1(DCH0_bcd0[1]), .BCD0(DCH0_bcd0[0]));
  BCD2LED bcd2led_4 (
    .B3(DCH0_bcd0[3]), .B2(DCH0_bcd0[2]), .B1(DCH0_bcd0[1]), .B0(DCH0_bcd0[0]), .a(bcd2led_4_a),
    .b(bcd2led_4_b), .c(bcd2led_4_c), .d(bcd2led_4_d), .e(bcd2led_4_e), .f(bcd2led_4_f), .g(bcd2led_4_g));
  _7_Segment_Display u_7_segment_display_4 (
    .g(bcd2led_4_g), .f(bcd2led_4_f), .a(bcd2led_4_a), .b(bcd2led_4_b), .e(bcd2led_4_e), .d(bcd2led_4_d),
    .c(bcd2led_4_c), .dp(1'b0));
  Hex_Digit_Display hex_digit_display_4 (.value(counter_4_q), .dp(1'b0));
  Counter #(.width(4), .max('h9)) counter_4 (
    .Q(counter_4_q), .clk(D0_out), .clr(D_out));  // open: load, D, count, carry
  Button D0 (.out(D0_out));
  D_Flip_Flop Q3_2 (.clk(out_2), .D(multiplexer_6_out), .Q(out_4[3]));  // open: Qn, preset, en, reset
  LED led_5 (.in(out_4[3]));
  LED led_6 (.in(d_ff_1_q));
  Button button_1 (.out(button_1_out));
  D_Flip_Flop Q2_2 (.clk(out_2), .D(multiplexer_7_out), .Q(out_4[2]));  // open: Qn, preset, en, reset
  Multiplexer multiplexer_6 (.in0(out_4[2]), .in1(1'b1), .out(multiplexer_6_out), .sel(in_1));  // open: en
  LED led_7 (.in(out_4[2]));
  D_Flip_Flop Q1_2 (.clk(out_2), .D(multiplexer_8_out), .Q(out_4[1]));  // open: Qn, preset, en, reset
  Multiplexer multiplexer_7 (.in0(out_4[1]), .in1(1'b1), .out(multiplexer_7_out), .sel(in_1));  // open: en
  Multiplexer multiplexer_8 (.in0(out_4[0]), .in1(1'b0), .out(multiplexer_8_out), .sel(in_1));  // open: en
  LED led_8 (.in(out_4[1]));
  D_Flip_Flop Q0_2 (.clk(out_2), .D(multiplexer_5_out), .Q(out_4[0]));  // open: Qn, preset, en, reset
  LED led_9 (.in(out_4[0]));
  Multiplexer multiplexer_9 (.in0(FL_3_out), .in1(1'b1), .out(multiplexer_9_out), .sel(in_1));  // open: en
  xor FL_3 (FL_3_out, out_5[3], out_5[2]);
  D_Flip_Flop Q3_3 (.clk(out_2), .D(multiplexer_10_out), .Q(out_5[3]));  // open: Qn, preset, en, reset
  Multiplexer multiplexer_10 (.in0(out_5[2]), .in1(1'b1), .out(multiplexer_10_out), .sel(in_1));  // open: en
  LED led_10 (.in(out_5[3]));
  D_Flip_Flop Q2_3 (.clk(out_2), .D(multiplexer_11_out), .Q(out_5[2]));  // open: Qn, preset, en, reset
  LED led_11 (.in(out_5[2]));
  D_Flip_Flop Q1_3 (.clk(out_2), .D(multiplexer_12_out), .Q(out_5[1]));  // open: Qn, preset, en, reset
  Multiplexer multiplexer_11 (.in0(out_5[1]), .in1(1'b0), .out(multiplexer_11_out), .sel(in_1));  // open: en
  Multiplexer multiplexer_12 (.in0(out_5[0]), .in1(1'b0), .out(multiplexer_12_out), .sel(in_1));  // open: en
  LED led_12 (.in(out_5[1]));
  D_Flip_Flop Q0_3 (.clk(out_2), .D(multiplexer_9_out), .Q(out_5[0]));  // open: Qn, preset, en, reset
  LED led_13 (.in(out_5[0]));
  // Probe on DCH3_bcd0
  and and_2 (and_2_out, comparator_1_eq, comparator_3_eq, comparator_2_eq, comparator_4_eq);
  // Probe on counter_1_q
  Multiplexer multiplexer_13 (.in0(FL_4_out), .in1(1'b0), .out(multiplexer_13_out), .sel(in_1));  // open: en
  // Probe on DCH2_bcd0
  Comparator #(.width(4)) comparator_1 (.a(DCH3_bcd0), .b(counter_1_q), .eq(comparator_1_eq));  // open: gt, lt
  // Probe on counter_2_q
  D_Flip_Flop Q3_4 (.clk(out_2), .D(multiplexer_14_out), .Q(out_6[3]));  // open: Qn, preset, en, reset
  xor FL_4 (FL_4_out, out_6[3], out_6[2]);
  // Probe on DCH1_bcd0
  // Probe on DCH0_bcd0
  Comparator #(.width(4)) comparator_2 (.a(DCH1_bcd0), .b(counter_3_q), .eq(comparator_2_eq));  // open: gt, lt
  Comparator #(.width(4)) comparator_3 (.a(DCH2_bcd0), .b(counter_2_q), .eq(comparator_3_eq));  // open: gt, lt
  // Probe on counter_3_q
  // Probe on counter_4_q
  Multiplexer multiplexer_14 (.in0(out_6[2]), .in1(1'b0), .out(multiplexer_14_out), .sel(in_1));  // open: en
  LED led_14 (.in(out_6[3]));
  Comparator #(.width(4)) comparator_4 (.a(DCH0_bcd0), .b(counter_4_q), .eq(comparator_4_eq));  // open: gt, lt
  D_Flip_Flop Q2_4 (.clk(out_2), .D(multiplexer_15_out), .Q(out_6[2]));  // open: Qn, preset, en, reset
  LED led_15 (.in(out_6[2]));
  D_Flip_Flop Q1_4 (.clk(out_2), .D(multiplexer_16_out), .Q(out_6[1]));  // open: Qn, preset, en, reset
  Multiplexer multiplexer_15 (.in0(out_6[1]), .in1(1'b1), .out(multiplexer_15_out), .sel(in_1));  // open: en
  LED led_16 (.in(out_6[1]));
  Multiplexer multiplexer_16 (.in0(out_6[0]), .in1(1'b1), .out(multiplexer_16_out), .sel(in_1));  // open: en
  D_Flip_Flop Q0_4 (.clk(out_2), .D(multiplexer_13_out), .Q(out_6[0]));  // open: Qn, preset, en, reset
  LED led_17 (.in(out_6[0]));

  // Notes on the sheet:
  //   Master Clock Input
  //   Reset/Start Button
  //   Generated OTP : 
  //   User Input : 
  //   Input Buttons (Press to Increment Value) :
  //   OTP Generator Sub-Circuit 3
  //   <- D Flip-Flop to hold the output untill submit button is pressed again
  //   Clock Distribution Bus
  //   Green -> Submitted OTP is Correct
  //   <- Submit Button
  //   OTP Generator Sub-Circuit 2
  //   To start this circuit :
  //   <- Output Indicator
  //   Red -> OTP Not Submitted Yet OR Submitted OTP is Incorrect 
  //   1. Go to Simulate>Check the "Tick Enabled" option.
  //   2. Keep the Reset button pressed until generated OTP changes from 0000.
  //   3. Enter the generated OTP in User Input and Validate using Submit Button  
  //   This circuit implements a hardware-based One-Time Password (OTP) generation and
  //   validation system using a 16-bit Linear Feedback Shift Register (LFSR) architecture.
  //   The system generates pseudo-random hexadecimal codes displayed on seven-
  //   segment displays and includes validation logic for authentication purposes.
  //   TRUE only when all the user inputted digits match with generated digits :
  //   OTP Generator Sub-Circuit 1
  //   Comparison Circuit :
  //   OTP Generator Sub-Circuit 0
endmodule

module BCD2LED (
  input  B3,
  input  B2,
  input  B1,
  input  B0,
  output a,
  output b,
  output c,
  output d,
  output e,
  output f,
  output g
);

  wire and_1_out, and_2_out, and_3_out, and_4_out, and_5_out, and_6_out, and_7_out, and_8_out, and_9_out,
       and_10_out, and_11_out, and_12_out, and_13_out, and_14_out, and_15_out, and_16_out, not_1_out,
       not_2_out, not_3_out, not_4_out, not_5_out, not_6_out, not_7_out, not_8_out, not_9_out, not_10_out,
       not_11_out, not_12_out, not_13_out, not_14_out, not_15_out, not_16_out, not_17_out, not_18_out,
       not_19_out, not_20_out, not_21_out;

  not not_1 (not_1_out, B2);
  and and_1 (and_1_out, not_1_out, not_2_out);
  not not_2 (not_2_out, B0);
  and and_2 (and_2_out, B2, B0);
  not not_3 (not_3_out, B2);
  not not_4 (not_4_out, B1);
  and and_3 (and_3_out, not_4_out, not_5_out);
  not not_5 (not_5_out, B0);
  and and_4 (and_4_out, B1, B0);
  not not_6 (not_6_out, B1);
  or or_1 (c, not_6_out, B0, B2);
  not not_7 (not_7_out, B2);
  and and_5 (and_5_out, not_7_out, not_8_out);
  not not_8 (not_8_out, B0);
  not not_9 (not_9_out, B2);
  and and_6 (and_6_out, not_9_out, B1);
  and and_7 (and_7_out, B1, not_10_out);
  not not_10 (not_10_out, B0);
  not not_11 (not_11_out, B1);
  and and_8 (and_8_out, B2, not_11_out, B0);
  not not_12 (not_12_out, B2);
  and and_9 (and_9_out, not_12_out, not_13_out);
  not not_13 (not_13_out, B0);
  and and_10 (and_10_out, B1, not_14_out);
  not not_14 (not_14_out, B0);
  not not_15 (not_15_out, B1);
  and and_11 (and_11_out, not_15_out, not_16_out);
  not not_16 (not_16_out, B0);
  and and_12 (and_12_out, B2, not_17_out);
  not not_17 (not_17_out, B1);
  and and_13 (and_13_out, B2, not_18_out);
  not not_18 (not_18_out, B0);
  not not_19 (not_19_out, B2);
  and and_14 (and_14_out, not_19_out, B1);
  and and_15 (and_15_out, B2, not_20_out);
  not not_20 (not_20_out, B1);
  and and_16 (and_16_out, B2, not_21_out);
  not not_21 (not_21_out, B0);
  or or_2 (a, and_1_out, B1, and_2_out, B3);
  or or_3 (b, not_3_out, and_3_out, and_4_out);
  or or_4 (d, and_5_out, and_6_out, and_7_out, and_8_out, B3);
  or or_5 (e, and_9_out, and_10_out);
  or or_6 (f, and_11_out, and_12_out, and_13_out, B3);
  or or_7 (g, and_14_out, and_15_out, and_16_out, B3);
endmodule

module DCHandling (
  input  B3,
  input  B2,
  input  B1,
  input  B0,
  output BCD3,
  output BCD2,
  output BCD1,
  output BCD0
);

  wire and_1_out, and_2_out, and_3_out, and_4_out, and_5_out, and_6_out, and_7_out, and_8_out, and_9_out,
       and_10_out, and_11_out, and_12_out, and_13_out, not_1_out, not_2_out, not_3_out, not_4_out, not_5_out,
       not_6_out, not_7_out, not_8_out, not_9_out, not_10_out, not_11_out, not_12_out, not_13_out, not_14_out;

  not not_1 (not_1_out, B2);
  and and_1 (and_1_out, B3, not_1_out, not_2_out);
  not not_2 (not_2_out, B1);
  and and_2 (and_2_out, B3, B2, B1, B0);
  not not_3 (not_3_out, B3);
  not not_4 (not_4_out, B1);
  not not_5 (not_5_out, B0);
  not not_6 (not_6_out, B2);
  not not_7 (not_7_out, B3);
  not not_8 (not_8_out, B0);
  not not_9 (not_9_out, B1);
  not not_10 (not_10_out, B3);
  not not_11 (not_11_out, B1);
  not not_12 (not_12_out, B2);
  not not_13 (not_13_out, B0);
  not not_14 (not_14_out, B1);
  or or_1 (BCD3, and_1_out, and_2_out);
  and and_3 (and_3_out, not_3_out, B2);
  and and_4 (and_4_out, B2, not_4_out);
  and and_5 (and_5_out, B2, not_5_out);
  and and_6 (and_6_out, B3, not_6_out, B1, B0);
  and and_7 (and_7_out, not_7_out, B1);
  or or_2 (BCD1, and_7_out, and_8_out, and_9_out);
  and and_8 (and_8_out, B1, not_8_out);
  and and_9 (and_9_out, B3, B2, not_9_out, B0);
  and and_10 (and_10_out, not_10_out, B0);
  and and_11 (and_11_out, not_11_out, B0);
  and and_12 (and_12_out, B3, not_12_out, B1, not_13_out);
  and and_13 (and_13_out, B3, B2, not_14_out);
  or or_3 (BCD2, and_3_out, and_4_out, and_5_out, and_6_out);
  or or_4 (BCD0, and_10_out, and_11_out, and_12_out, and_13_out);
endmodule

// DCsH
module DCHandlingFixed (
  input  B0,
  input  B1,
  input  B2,
  input  B3,
  output BCD3,
  output BCD2,
  output BCD1,
  output BCD0
);

  wire and_1_out, and_2_out, and_3_out, and_4_out, and_5_out, and_6_out, and_7_out, and_8_out, and_9_out,
       and_10_out, and_11_out, and_12_out, and_13_out, not_1_out, not_2_out, not_3_out, not_4_out, not_5_out,
       not_6_out, not_7_out, not_8_out, not_9_out, not_10_out, not_11_out, not_12_out, not_13_out, not_14_out;

  not not_1 (not_1_out, B2);
  and and_1 (and_1_out, B3, not_1_out, not_2_out);
  not not_2 (not_2_out, B1);
  and and_2 (and_2_out, B3, B2, B1, B0);
  not not_3 (not_3_out, B3);
  not not_4 (not_4_out, B1);
  not not_5 (not_5_out, B0);
  not not_6 (not_6_out, B2);
  not not_7 (not_7_out, B3);
  not not_8 (not_8_out, B0);
  not not_9 (not_9_out, B1);
  not not_10 (not_10_out, B3);
  not not_11 (not_11_out, B1);
  not not_12 (not_12_out, B2);
  not not_13 (not_13_out, B0);
  not not_14 (not_14_out, B1);
  or or_1 (BCD3, and_1_out, and_2_out);
  and and_3 (and_3_out, not_3_out, B2);
  and and_4 (and_4_out, B2, not_4_out);
  and and_5 (and_5_out, B2, not_5_out);
  and and_6 (and_6_out, B3, not_6_out, B1, B0);
  and and_7 (and_7_out, not_7_out, B1);
  or or_2 (BCD1, and_7_out, and_8_out, and_9_out);
  and and_8 (and_8_out, B1, not_8_out);
  and and_9 (and_9_out, B3, B2, not_9_out, B0);
  and and_10 (and_10_out, not_10_out, B0);
  and and_11 (and_11_out, not_11_out, B0);
  and and_12 (and_12_out, B3, not_12_out, B1, not_13_out);
  and and_13 (and_13_out, B3, B2, not_14_out);
  or or_3 (BCD2, and_3_out, and_4_out, and_5_out, and_6_out);
  or or_4 (BCD0, and_10_out, and_11_out, and_12_out, and_13_out);
endmodule
